// Logisim project 4bitcomp_using_only_not.circ as structural Verilog: 4 circuits, main circuit main
module main (
  input  A3,
  input  B3,
  input  A2,
  input  B2,
  input  A1,
  input  B1,
  input  A0,
  input  B0,
  output Equal,
  output Aless,
  output Agreater
);

  wire and_using_nor_1_z, and_using_nor_2_z, and_using_nor_3_z, and_using_nor_4_z, and_using_nor_5_z,
       and_using_nor_6_z, and_using_nor_7_z, and_using_nor_8_z, and_using_nor_9_z, nor_1_out, nor_2_out,
       nor_3_out, nor_4_out, or_using_nor_1_z, or_using_nor_2_z, or_using_nor_4_z, xnor_using_nor_1_z,
       xnor_using_nor_2_z, xnor_using_nor_3_z, xnor_using_nor_4_z;

  nor nor_1 (nor_1_out, B3, B3);
  nor nor_2 (nor_2_out, B2, B2);
  nor nor_3 (nor_3_out, B1, B1);
  nor nor_4 (nor_4_out, B0, B0);
  and_using_nor and_using_nor_1 (.X(A2), .Y(nor_2_out), .Z(and_using_nor_1_z));
  and_using_nor and_using_nor_2 (.X(A1), .Y(nor_3_out), .Z(and_using_nor_2_z));
  and_using_nor and_using_nor_3 (.X(A0), .Y(nor_4_out), .Z(and_using_nor_3_z));
  xnor_using_nor xnor_using_nor_1 (.X(A3), .Y(B3), .Z(xnor_using_nor_1_z));
  xnor_using_nor xnor_using_nor_2 (.X(A2), .Y(B2), .Z(xnor_using_nor_2_z));
  xnor_using_nor xnor_using_nor_3 (.X(A1), .Y(B1), .Z(xnor_using_nor_3_z));
  xnor_using_nor xnor_using_nor_4 (.X(A0), .Y(B0), .Z(xnor_using_nor_4_z));
  and_using_nor and_using_nor_4 (.X(A3), .Y(nor_1_out), .Z(and_using_nor_4_z));
  and_using_nor and_using_nor_5 (.X(xnor_using_nor_1_z), .Y(and_using_nor_1_z), .Z(and_using_nor_5_z));
  and_using_nor and_using_nor_6 (.X(xnor_using_nor_2_z), .Y(and_using_nor_2_z), .Z(and_using_nor_6_z));
  and_using_nor and_using_nor_7 (.X(xnor_using_nor_3_z), .Y(and_using_nor_3_z), .Z(and_using_nor_7_z));
  and_using_nor and_using_nor_8 (.X(xnor_using_nor_1_z), .Y(xnor_using_nor_2_z), .Z(and_using_nor_8_z));
  and_using_nor and_using_nor_9 (.X(xnor_using_nor_3_z), .Y(xnor_using_nor_4_z), .Z(and_using_nor_9_z));
  or_using_nor or_using_nor_1 (.X(and_using_nor_4_z), .Y(and_using_nor_5_z), .Z(or_using_nor_1_z));
  or_using_nor or_using_nor_2 (.X(and_using_nor_6_z), .Y(and_using_nor_7_z), .Z(or_using_nor_2_z));
  and_using_nor and_using_nor_10 (.X(and_using_nor_8_z), .Y(and_using_nor_9_z), .Z(Equal));
  or_using_nor or_using_nor_3 (.X(or_using_nor_1_z), .Y(or_using_nor_2_z), .Z(Agreater));
  or_using_nor or_using_nor_4 (.X(Equal), .Y(Agreater), .Z(or_using_nor_4_z));
  nor nor_5 (Aless, or_using_nor_4_z, or_using_nor_4_z);
endmodule

module and_using_nor (
  input  X,
  input  Y,
  output Z
);

  wire nor_1_out, nor_2_out;

  nor nor_1 (nor_1_out, X, X);
  nor nor_2 (nor_2_out, Y, Y);
  nor nor_3 (Z, nor_1_out, nor_2_out);
endmodule

module or_using_nor (
  input  X,
  input  Y,
  output Z
);

  wire nor_1_out;

  nor nor_1 (nor_1_out, X, Y);
  nor nor_2 (Z, nor_1_out, nor_1_out);
endmodule

module xnor_using_nor (
  input  X,
  input  Y,
  output Z
);

  wire and_using_nor_1_z, and_using_nor_2_z, nor_1_out, nor_2_out, or_using_nor_1_z;

  nor nor_1 (nor_1_out, X, X);
  nor nor_2 (nor_2_out, Y, Y);
  and_using_nor and_using_nor_1 (.X(nor_1_out), .Y(Y), .Z(and_using_nor_1_z));
  and_using_nor and_using_nor_2 (.X(X), .Y(nor_2_out), .Z(and_using_nor_2_z));
  or_using_nor or_using_nor_1 (.X(and_using_nor_1_z), .Y(and_using_nor_2_z), .Z(or_using_nor_1_z));
  nor nor_3 (Z, or_using_nor_1_z, or_using_nor_1_z);
endmodule
