// Logisim project Carry_look_ahead.circ as structural Verilog: 2 circuits, main circuit main
module main (
  input  C0,
  input  in_2,
  input  in_3,
  input  in_4,
  input  in_5,
  input  in_6,
  input  in_7,
  input  in_8,
  input  in_9,
  output S0,
  output C1,
  output S1,
  output C2,
  output S2,
  output C3,
  output S3,
  output C4
);

  wire and_1_out, and_2_out, and_3_out, and_4_out, and_5_out, and_6_out, and_7_out, and_8_out, and_9_out,
       and_10_out, p_g_1_g0, p_g_1_g1, p_g_1_g2, p_g_1_g3, p_g_1_p0, p_g_1_p1, p_g_1_p2, p_g_1_p3;

  P_G p_g_1 (
    .A0(in_2), .B0(in_3), .A1(in_4), .B1(in_5), .A2(in_6), .B2(in_7), .A3(in_8), .B3(in_9), .P0(p_g_1_p0),
    .G0(p_g_1_g0), .P1(p_g_1_p1), .G1(p_g_1_g1), .P2(p_g_1_p2), .G2(p_g_1_g2), .P3(p_g_1_p3), .G3(p_g_1_g3));
  and and_1 (and_1_out, C0, p_g_1_p0);
  and and_2 (and_2_out, p_g_1_g0, p_g_1_p1);
  and and_3 (and_3_out, and_1_out, p_g_1_p1);
  and and_4 (and_4_out, p_g_1_p2, p_g_1_g1);
  and and_5 (and_5_out, and_2_out, p_g_1_p2);
  and and_6 (and_6_out, and_3_out, p_g_1_p2);
  and and_7 (and_7_out, p_g_1_p3, p_g_1_g2);
  and and_8 (and_8_out, and_4_out, p_g_1_p3);
  and and_9 (and_9_out, and_5_out, p_g_1_p3);
  and and_10 (and_10_out, and_6_out, p_g_1_p3);
  or or_1 (C1, and_1_out, p_g_1_g0);
  or or_2 (C2, and_2_out, p_g_1_g1, and_3_out);
  or or_3 (C3, p_g_1_g2, and_4_out, and_5_out, and_6_out);
  or or_4 (C4, p_g_1_g3, and_7_out, and_8_out, and_9_out, and_10_out);
  xor xor_1 (S0, C0, p_g_1_p0);
  xor xor_2 (S1, C1, p_g_1_p1);
  xor xor_3 (S2, C2, p_g_1_p2);
  xor xor_4 (S3, C3, p_g_1_p3);
endmodule

module P_G (
  input  A0,
  input  B0,
  input  A1,
  input  B1,
  input  A2,
  input  B2,
  input  A3,
  input  B3,
  output P0,
  output G0,
  output P1,
  output G1,
  output P2,
  output G2,
  output P3,
  output G3
);

  xor xor_1 (P0, A0, B0);
  and and_1 (G0, A0, B0);
  xor xor_2 (P1, A1, B1);
  and and_2 (G1, A1, B1);
  xor xor_3 (P2, A2, B2);
  and and_3 (G2, A2, B2);
  xor xor_4 (P3, A3, B3);
  and and_4 (G3, A3, B3);

  // Notes on the sheet:
  //   A0
  //   B0
  //   A1
  //   B1
  //   A2
  //   B2
endmodule
